// Logisim project project.circ as structural Verilog: 9 circuits, main circuit main
module main (
);

  wire and_3_out, and_4_out, and_5_out, button_2_out, button_3_out, button_4_out, button_5_out, button_6_out,
       button_7_out, button_8_out, button_9_out, button_10_out, c1, c2, c3, c4, c5, c6, c7, c8, c9,
       cdm_8_mark5_1_data_inst, Cl, Code, data, f1, f2, f3, f4, f5, f6, f7, f8, f9, I_Osel, In_out_prime,
       mem, nand_1_out, not_1_out, not_2_out, RAM, reset, tc, win_1_o_win, win_1_tie, win_1_x_win, x;
  wire [3:0] dm_1__1_out, dm_1__2_out, dm_1__3_out, dm_1__4_out, dm_2__1_out, dm_2__2_out, dm_2__3_out,
       dm_2__4_out, dm_3__1_out, dm_3__2_out, dm_3__3_out, dm_3__4_out, dm_4__1_out, dm_4__2_out,
       dm_4__3_out, dm_4__4_out, dm_5__1_out, dm_5__2_out, dm_5__3_out, dm_5__4_out, dm_6__1_out,
       dm_6__2_out, dm_6__3_out, dm_6__4_out, dm_7__1_out, dm_7__2_out, dm_7__3_out, dm_7__4_out,
       dm_8__1_out, dm_8__2_out, dm_8__3_out, dm_8__4_out, dm_9__1_out, dm_9__2_out, dm_9__3_out,
       dm_9__4_out, I_Oadr, p1, p2, p3, p4, p5, p6, p7, p8, p9;
  wire [7:0] cdm_8_mark5_1_data_out, cdm_8_mark5_1_pc, cdm_8_mark5_1_ps, cdm_8_mark5_1_r0, cdm_8_mark5_1_r1,
       cdm_8_mark5_1_r2, cdm_8_mark5_1_r3, cdm_8_mark5_1_sp, controlled_buffer_1_out, I_Odat;
  wire [7:4] cdm_8_mark5_1_addr;

  PSC psc_1 (
    ._1_cell(f1), ._2_cell(f2), ._3_cell(f3), ._4_cell(f4), ._5_cell(f5), ._6_cell(f6), ._7_cell(f7),
    ._8_cell(f8), ._9_cell(f9), .select_player(x), .reset(reset));
  LED O_win (.in(win_1_o_win));
  LED Current_Player__Green_O_Black_X (.in(x));
  LED Tie (.in(win_1_tie));
  LED X_win (.in(win_1_x_win));
  Button button_1 (.out(reset));
  win win_1 (
    ._1_in(p1), ._2_in(p2), ._3_in(p3), ._4_in(p4), ._5_in(p5), ._6_in(p6), ._7_in(p7), ._8_in(p8),
    ._9_in(p9), .O_win(win_1_o_win), .X_win(win_1_x_win), .Tie(win_1_tie), .Trun_controll(tc));
  and and_1 (I_Osel, not_1_out, Cl, data);
  // Probe on cdm_8_mark5_1_r1
  // Probe on cdm_8_mark5_1_r2
  // Probe on cdm_8_mark5_1_r0
  // Probe on cdm_8_mark5_1_r3
  // Probe on cdm_8_mark5_1_pc
  Clock clock_1 (.out(Cl));
  not not_1 (not_1_out, nand_1_out);
  and and_2 (RAM, nand_1_out, data);
  Button button_2 (.out(button_2_out));
  bcc bcc_1 (.can_turn__0_can_1_can_t(tc), .btn(button_2_out), .turn(f1), .mark_cell(p1), .cpu(c1));
  bcc bcc_2 (.can_turn__0_can_1_can_t(tc), .btn(button_3_out), .turn(f4), .mark_cell(p4), .cpu(c4));
  Button button_3 (.out(button_3_out));
  Button button_4 (.out(button_4_out));
  bcc bcc_3 (.can_turn__0_can_1_can_t(tc), .btn(button_4_out), .turn(f7), .mark_cell(p7), .cpu(c7));
  // Probe on cdm_8_mark5_1_sp
  // Probe on cdm_8_mark5_1_ps
  CdM_8_mark5 cdm_8_mark5_1 (
    .clock(Cl), .addr({cdm_8_mark5_1_addr, I_Oadr}), .mem_read(In_out_prime), .mem_cycle(mem),
    .data_inst(cdm_8_mark5_1_data_inst), .data_out(cdm_8_mark5_1_data_out),
    .data_in(controlled_buffer_1_out), .r0(cdm_8_mark5_1_r0), .r1(cdm_8_mark5_1_r1), .r2(cdm_8_mark5_1_r2),
    .r3(cdm_8_mark5_1_r3), .PC(cdm_8_mark5_1_pc), .SP(cdm_8_mark5_1_sp), .PS(cdm_8_mark5_1_ps), .reset(reset));  // open: IAck, IRQ, vec
  nand nand_1 (nand_1_out, cdm_8_mark5_1_addr[4], cdm_8_mark5_1_addr[5], cdm_8_mark5_1_addr[6], cdm_8_mark5_1_addr[7]);
  DM dm_1 (
    .Player(x), .Turn(f1), ._1_out(dm_1__1_out), ._2_out(dm_1__2_out), ._3_out(dm_1__3_out),
    ._4_out(dm_1__4_out), .player_out(p1), .reset(reset));
  DotMatrix #(.inputtype("row"), .matrixcols(4), .matrixrows(4)) dotmatrix_1 (
    .row0(dm_1__1_out), .row1(dm_1__2_out), .row2(dm_1__3_out), .row3(dm_1__4_out));
  DotMatrix #(.inputtype("row"), .matrixcols(4), .matrixrows(4)) dotmatrix_2 (
    .row0(dm_2__1_out), .row1(dm_2__2_out), .row2(dm_2__3_out), .row3(dm_2__4_out));
  DM dm_2 (
    .Player(x), .Turn(f4), ._1_out(dm_2__1_out), ._2_out(dm_2__2_out), ._3_out(dm_2__3_out),
    ._4_out(dm_2__4_out), .player_out(p4), .reset(reset));
  DM dm_3 (
    .Player(x), .Turn(f7), ._1_out(dm_3__1_out), ._2_out(dm_3__2_out), ._3_out(dm_3__3_out),
    ._4_out(dm_3__4_out), .player_out(p7), .reset(reset));
  DotMatrix #(.inputtype("row"), .matrixcols(4), .matrixrows(4)) dotmatrix_3 (
    .row0(dm_3__1_out), .row1(dm_3__2_out), .row2(dm_3__3_out), .row3(dm_3__4_out));
  assign controlled_buffer_1_out = In_out_prime ? I_Odat : 8'bz;  // Controlled_Buffer controlled_buffer_1
  Button button_5 (.out(button_5_out));
  bcc bcc_4 (.can_turn__0_can_1_can_t(tc), .btn(button_5_out), .turn(f2), .mark_cell(p2), .cpu(c2));
  bcc bcc_5 (.can_turn__0_can_1_can_t(tc), .btn(button_6_out), .turn(f5), .mark_cell(p5), .cpu(c5));
  Button button_6 (.out(button_6_out));
  Button button_7 (.out(button_7_out));
  bcc bcc_6 (.can_turn__0_can_1_can_t(tc), .btn(button_7_out), .turn(f8), .mark_cell(p8), .cpu(c8));
  Decoder #(.disabled(0)) decoder_1 (.out0(Code), .out1(data), .sel(cdm_8_mark5_1_data_inst), .en(mem));
  assign I_Odat = not_2_out ? cdm_8_mark5_1_data_out : 8'bz;  // Controlled_Buffer controlled_buffer_2
  not not_2 (not_2_out, In_out_prime);
  DotMatrix #(.inputtype("row"), .matrixcols(4), .matrixrows(4)) dotmatrix_4 (
    .row0(dm_4__1_out), .row1(dm_4__2_out), .row2(dm_4__3_out), .row3(dm_4__4_out));
  DM dm_4 (
    .Player(x), .Turn(f2), ._1_out(dm_4__1_out), ._2_out(dm_4__2_out), ._3_out(dm_4__3_out),
    ._4_out(dm_4__4_out), .player_out(p2), .reset(reset));
  DotMatrix #(.inputtype("row"), .matrixcols(4), .matrixrows(4)) dotmatrix_5 (
    .row0(dm_5__1_out), .row1(dm_5__2_out), .row2(dm_5__3_out), .row3(dm_5__4_out));
  DM dm_5 (
    .Player(x), .Turn(f5), ._1_out(dm_5__1_out), ._2_out(dm_5__2_out), ._3_out(dm_5__3_out),
    ._4_out(dm_5__4_out), .player_out(p5), .reset(reset));
  DotMatrix #(.inputtype("row"), .matrixcols(4), .matrixrows(4)) dotmatrix_6 (
    .row0(dm_6__1_out), .row1(dm_6__2_out), .row2(dm_6__3_out), .row3(dm_6__4_out));
  DM dm_6 (
    .Player(x), .Turn(f8), ._1_out(dm_6__1_out), ._2_out(dm_6__2_out), ._3_out(dm_6__3_out),
    ._4_out(dm_6__4_out), .player_out(p8), .reset(reset));
  Pull_Resistor pull_resistor_1 (.node(I_Oadr[0]));
  Pull_Resistor pull_resistor_2 (.node(I_Oadr[1]));
  Pull_Resistor pull_resistor_3 (.node(I_Oadr[2]));
  Pull_Resistor pull_resistor_4 (.node(I_Oadr[3]));
  Pull_Resistor pull_resistor_5 (.node(cdm_8_mark5_1_addr[4]));
  Pull_Resistor pull_resistor_6 (.node(cdm_8_mark5_1_addr[5]));
  Pull_Resistor pull_resistor_7 (.node(cdm_8_mark5_1_addr[6]));
  Pull_Resistor pull_resistor_8 (.node(cdm_8_mark5_1_addr[7]));
  Button button_8 (.out(button_8_out));
  bcc bcc_7 (.can_turn__0_can_1_can_t(tc), .btn(button_8_out), .turn(f3), .mark_cell(p3), .cpu(c3));
  Button button_9 (.out(button_9_out));
  bcc bcc_8 (.can_turn__0_can_1_can_t(tc), .btn(button_9_out), .turn(f6), .mark_cell(p6), .cpu(c6));
  Button button_10 (.out(button_10_out));
  bcc bcc_9 (.can_turn__0_can_1_can_t(tc), .btn(button_10_out), .turn(f9), .mark_cell(p9), .cpu(c9));
  DM dm_7 (
    .Player(x), .Turn(f3), ._1_out(dm_7__1_out), ._2_out(dm_7__2_out), ._3_out(dm_7__3_out),
    ._4_out(dm_7__4_out), .player_out(p3), .reset(reset));
  DotMatrix #(.inputtype("row"), .matrixcols(4), .matrixrows(4)) dotmatrix_7 (
    .row0(dm_7__1_out), .row1(dm_7__2_out), .row2(dm_7__3_out), .row3(dm_7__4_out));
  DotMatrix #(.inputtype("row"), .matrixcols(4), .matrixrows(4)) dotmatrix_8 (
    .row0(dm_8__1_out), .row1(dm_8__2_out), .row2(dm_8__3_out), .row3(dm_8__4_out));
  DM dm_8 (
    .Player(x), .Turn(f6), ._1_out(dm_8__1_out), ._2_out(dm_8__2_out), ._3_out(dm_8__3_out),
    ._4_out(dm_8__4_out), .player_out(p6), .reset(reset));
  DotMatrix #(.inputtype("row"), .matrixcols(4), .matrixrows(4)) dotmatrix_9 (
    .row0(dm_9__1_out), .row1(dm_9__2_out), .row2(dm_9__3_out), .row3(dm_9__4_out));
  DM dm_9 (
    .Player(x), .Turn(f9), ._1_out(dm_9__1_out), ._2_out(dm_9__2_out), ._3_out(dm_9__3_out),
    ._4_out(dm_9__4_out), .player_out(p9), .reset(reset));
  ROM rom_1 (.addr({cdm_8_mark5_1_addr, I_Oadr}), .data(I_Odat), .sel(Code));
  RAM ram_1 (.addr({cdm_8_mark5_1_addr, I_Oadr}), .data(I_Odat), .sel(RAM), .clk(Cl), .ld(In_out_prime));  // open: clr
  and and_3 (and_3_out, ~I_Oadr[3], ~I_Oadr[2], ~I_Oadr[1], I_Oadr[0], I_Osel);  // AND_Gate
  FieldToCDM8 fieldtocdm8_1 (
    .to_cdm8(I_Odat), .reset(reset), ._1_in(p1), ._2_in(p2), ._3_in(p3), ._4_in(p4), ._5_in(p5), ._6_in(p6),
    ._7_in(p7), ._8_in(p8), ._9_in(p9), .write_state_to_cmd8(and_3_out), .read_write(In_out_prime));
  and and_4 (and_4_out, ~I_Oadr[3], ~I_Oadr[2], I_Oadr[1], ~I_Oadr[0], I_Osel);  // AND_Gate
  CDM8Turn cdm8turn_1 (
    .addr(and_4_out), .CDM8_input(I_Odat), .write(In_out_prime), .cell_1(c1), .cell_2(c2), .cell_3(c3),
    .cell_4(c4), .cell_5(c5), .cell_6(c6), .cell_7(c7), .cell_8(c8), .cell_9(c9));
  PlayerToCDM8 playertocdm8_1 (.addr(and_5_out), .read(In_out_prime), .player(x), .ToCDM8(I_Odat));
  and and_5 (and_5_out, ~I_Oadr[3], ~I_Oadr[2], I_Oadr[1], I_Oadr[0], I_Osel);  // AND_Gate

  // Other names for the same wires on the sheet: rd_wr_prime = In_out_prime

  // Notes on the sheet:
  //   data
  //   mem
  //   rd
  //   Аdr
  //   contents of rom_1 (hex, n*v repeats v):
  //   d0 0 0 e1 11 d0 f3 b0 d1 1 74 e1 f d6 12 ee 0 d4 d0 0 d1 8 71 e0 23 d1 3c 11 d2 f1 ba a6 8c ee 14 d0
  //   0 d1 8 71 e0 39 d1 3c 11 b5 5 e1 36 d2 f2 a8 ee 39 8c ee 25 d7 d6
endmodule

module MUX (
  input  [15:0] Input_0,
  input  sel,
  input  [15:0] Input_1,
  output [15:0] Output
);

  wire [15:0] and_1_out, and_2_out;
  wire [15:15] not_1_out;

  not not_1 (not_1_out[15], sel);
  assign and_1_out = Input_0 & {16{not_1_out[15]}};  // AND_Gate and_1, 16 bits wide
  assign and_2_out = {16{sel}} & Input_1;  // AND_Gate and_2, 16 bits wide
  assign Output = and_1_out | and_2_out;  // OR_Gate or_1, 16 bits wide
endmodule

module DM (
  input  reset,
  input  Player,
  input  Turn,
  output [3:0] player_out,
  output [3:0] _1_out,
  output [3:0] _2_out,
  output [3:0] _3_out,
  output [3:0] _4_out
);

  wire and_1_out, and_2_out, x1;
  wire [15:0] not_1_out, not_2_out, register_1_q, x2;

  assign not_1_out = ~16'h9429;  // NOT_Gate not_1, 16 bits wide
  assign not_2_out = ~16'hf99f;  // NOT_Gate not_2, 16 bits wide
  MUX mux_1 (.Input_0(not_1_out), .sel(Player), .Input_1(not_2_out), .Output(x2));
  and and_1 (and_1_out, Turn, ~x1);  // AND_Gate
  Register #(.width(16)) register_1 (.D(x2), .Q(register_1_q), .clk(and_2_out), .clr(reset));  // open: en
  and and_2 (and_2_out, Turn, ~x1);  // AND_Gate
  Register #(.width(1)) register_2 (.D(Turn), .Q(x1), .clk(and_1_out), .clr(reset));  // open: en
  Pull_Resistor pull_resistor_1 (.node({_4_out, _3_out, _2_out, _1_out}));
  assign {_4_out, _3_out, _2_out, _1_out} = x1 ? ~register_1_q : 16'bz;  // Controlled_Inverter controlled_inverter_1

  assign player_out = _1_out;

  // Other names for the same wires on the sheet: rest = reset

  // Notes on the sheet:
  //   Save player
  //   Save state
  //   Display outputs
endmodule

// WIN
module win (
  input  [3:0] _1_in,
  input  [3:0] _2_in,
  input  [3:0] _3_in,
  input  [3:0] _4_in,
  input  [3:0] _5_in,
  input  [3:0] _6_in,
  input  [3:0] _7_in,
  input  [3:0] _8_in,
  input  [3:0] _9_in,
  output O_win,
  output X_win,
  output Tie,
  output Trun_controll
);

  wire _1, _2, _3, _4, _5, _6, _7, _8, _9, and_1_out, and_2_out, and_3_out, and_4_out, and_14_out,
       and_15_out, and_16_out, and_17_out, and_18_out, and_19_out, and_20_out, and_21_out, and_22_out,
       and_23_out, and_24_out, and_25_out, and_26_out, transistor_1_out;

  Transistor transistor_1 (.in(transistor_1_out), .out(transistor_1_out), .gate(1'b1));
  and and_1 (and_1_out, _1_in[1], _2_in[1], _3_in[1]);
  and and_2 (and_2_out, _4_in[1], _5_in[1], _6_in[1]);
  and and_3 (and_3_out, _7_in[1], _8_in[1], _9_in[1]);
  and and_4 (and_4_out, _1_in[1], _4_in[1], _7_in[1]);
  and and_5 (_1, ~_1_in[1], _1_in[0]);  // AND_Gate
  and and_6 (_2, ~_2_in[1], _2_in[0]);  // AND_Gate
  and and_7 (_3, ~_3_in[1], _3_in[0]);  // AND_Gate
  and and_8 (_4, ~_4_in[1], _4_in[0]);  // AND_Gate
  and and_9 (_5, ~_5_in[1], _5_in[0]);  // AND_Gate
  and and_10 (_6, ~_6_in[1], _6_in[0]);  // AND_Gate
  and and_11 (_7, ~_7_in[1], _7_in[0]);  // AND_Gate
  and and_12 (_8, ~_8_in[1], _8_in[0]);  // AND_Gate
  and and_13 (_9, ~_9_in[1], _9_in[0]);  // AND_Gate
  and and_14 (and_14_out, _2_in[1], _5_in[1], _8_in[1]);
  and and_15 (and_15_out, _3_in[1], _6_in[1], _9_in[1]);
  and and_16 (and_16_out, _1_in[1], _5_in[1], _9_in[1]);
  and and_17 (and_17_out, _3_in[1], _5_in[1], _7_in[1]);
  or or_1 (O_win, and_1_out, and_2_out, and_3_out, and_4_out, and_14_out, and_15_out, and_16_out, and_17_out);
  and and_18 (and_18_out, _1, _2, _3);
  and and_19 (and_19_out, _4, _5, _6);
  and and_20 (and_20_out, _7, _8, _9);
  and and_21 (and_21_out, _1_in[0], _2_in[0], _3_in[0], _4_in[0], _5_in[0], _6_in[0], _7_in[0], _8_in[0], _9_in[0]);
  and and_22 (and_22_out, _1, _4, _7);
  and and_23 (and_23_out, _2, _5, _8);
  and and_24 (and_24_out, _3, _6, _9);
  or or_2 (Trun_controll, X_win, O_win, Tie);
  and and_25 (and_25_out, _1, _5, _9);
  and and_26 (and_26_out, _3, _5, _7);
  and and_27 (Tie, ~X_win, ~O_win, and_21_out);  // AND_Gate
  or or_3 (X_win, and_18_out, and_19_out, and_20_out, and_22_out, and_23_out, and_24_out, and_25_out, and_26_out);
  // also tied to VCC on the sheet: transistor_1_out

  // Other names for the same wires on the sheet: _1v0 = _1_in[0]; _1v = _1_in[1]; _2v0 = _2_in[0]; _2v = _2_in[1];
  //   _3v0 = _3_in[0]; _3v = _3_in[1]; _4v0 = _4_in[0]; _4v = _4_in[1]; _5v0 = _5_in[0]; _5v = _5_in[1];
  //   _6v0 = _6_in[0]; _6v = _6_in[1]; _7v0 = _7_in[0]; _7v = _7_in[1]; _8v0 = _8_in[0]; _8v = _8_in[1];
  //   _9v0 = _9_in[0]; _9v = _9_in[1]

  // Notes on the sheet:
  //   O win horizont combination
  //   O vertical combination
  //   O diagonal combination
  //   O win controll
  //   Enable turn buttons. 0 enable 1disable 
  //   X win controll
  //   Tie
endmodule

module bcc (
  input  [3:0] mark_cell,
  input  can_turn__0_can_1_can_t,
  input  btn,
  input  cpu,
  output turn
);

  wire or_1_out, or_2_out;

  or or_1 (or_1_out, btn, cpu);
  or or_2 (or_2_out, can_turn__0_can_1_can_t, mark_cell[0]);
  Transistor transistor_1 (.in(or_1_out), .out(turn), .gate(or_2_out));
  Pull_Resistor pull_resistor_1 (.node(turn));
endmodule

// Player sel
module PSC (
  input  _1_cell,
  input  _2_cell,
  input  _3_cell,
  input  _4_cell,
  input  _5_cell,
  input  _6_cell,
  input  reset,
  input  _7_cell,
  input  _8_cell,
  input  _9_cell,
  output select_player
);

  wire not_1_out, or_1_out;

  or or_1 (or_1_out, _1_cell, _2_cell, _3_cell, _4_cell, _5_cell, _6_cell, _7_cell, _8_cell, _9_cell);
  not not_1 (not_1_out, select_player);
  Register #(.width(1)) register_1 (.D(not_1_out), .Q(select_player), .clk(or_1_out), .clr(reset));  // open: en
endmodule

module FieldToCDM8 (
  input  [3:0] _1_in,
  input  [3:0] _2_in,
  input  read_write,
  input  [3:0] _3_in,
  input  [3:0] _4_in,
  input  [3:0] _5_in,
  input  [3:0] _6_in,
  input  [3:0] _7_in,
  input  [3:0] _8_in,
  input  [3:0] _9_in,
  input  reset,
  input  write_state_to_cmd8,
  output [7:0] to_cdm8
);

  wire _1, _2, _3, _4, _5, _6, _7, _8, _9, decoder_1_out1, r0, r1, r2, r3, r4, r5, r6, r7, r8,
       transistor_1_out;
  wire [3:0] counter_1_q;
  wire [7:0] and_10_out, and_11_out, and_12_out, and_13_out, and_14_out, and_15_out, and_16_out, and_17_out,
       and_18_out, and_19_out, and_20_out, and_21_out, and_22_out, and_23_out, and_24_out, and_25_out,
       and_26_out, and_27_out, multiplexer_1_out, or_1_out, or_2_out, or_3_out, or_4_out, or_5_out, or_6_out,
       or_7_out, or_8_out, or_9_out, register_1_q, register_2_q, register_3_q, register_4_q, register_5_q,
       register_6_q, register_7_q, register_8_q, register_9_q;

  Transistor transistor_1 (.in(transistor_1_out), .out(transistor_1_out));  // open: gate
  and and_1 (_1, ~_1_in[1], _1_in[0]);  // AND_Gate
  and and_2 (_2, ~_2_in[1], _2_in[0]);  // AND_Gate
  and and_3 (_3, ~_3_in[1], _3_in[0]);  // AND_Gate
  and and_4 (_4, ~_4_in[1], _4_in[0]);  // AND_Gate
  and and_5 (_5, ~_5_in[1], _5_in[0]);  // AND_Gate
  and and_6 (_6, ~_6_in[1], _6_in[0]);  // AND_Gate
  and and_7 (_7, ~_7_in[1], _7_in[0]);  // AND_Gate
  and and_8 (_8, ~_8_in[1], _8_in[0]);  // AND_Gate
  and and_9 (_9, ~_9_in[1], _9_in[0]);  // AND_Gate
  assign and_10_out = {8{_1}} & 8'h2;  // AND_Gate and_10, 8 bits wide
  assign and_11_out = {8{_1_in[1]}} & 8'h3;  // AND_Gate and_11, 8 bits wide
  assign and_12_out = {8{_2}} & 8'h2;  // AND_Gate and_12, 8 bits wide
  assign and_13_out = {8{_2_in[1]}} & 8'h3;  // AND_Gate and_13, 8 bits wide
  assign and_14_out = {8{_3}} & 8'h2;  // AND_Gate and_14, 8 bits wide
  assign and_15_out = {8{_3_in[1]}} & 8'h3;  // AND_Gate and_15, 8 bits wide
  assign and_16_out = {8{_4}} & 8'h2;  // AND_Gate and_16, 8 bits wide
  assign and_17_out = {8{_4_in[1]}} & 8'h3;  // AND_Gate and_17, 8 bits wide
  assign and_18_out = {8{_5}} & 8'h2;  // AND_Gate and_18, 8 bits wide
  assign and_19_out = {8{_5_in[1]}} & 8'h3;  // AND_Gate and_19, 8 bits wide
  assign and_20_out = {8{_6}} & 8'h2;  // AND_Gate and_20, 8 bits wide
  assign and_21_out = {8{_6_in[1]}} & 8'h3;  // AND_Gate and_21, 8 bits wide
  assign and_22_out = {8{_7}} & 8'h2;  // AND_Gate and_22, 8 bits wide
  assign and_23_out = {8{_7_in[1]}} & 8'h3;  // AND_Gate and_23, 8 bits wide
  assign and_24_out = {8{_8}} & 8'h2;  // AND_Gate and_24, 8 bits wide
  assign and_25_out = {8{_8_in[1]}} & 8'h3;  // AND_Gate and_25, 8 bits wide
  assign and_26_out = {8{_9}} & 8'h2;  // AND_Gate and_26, 8 bits wide
  assign and_27_out = {8{_9_in[1]}} & 8'h3;  // AND_Gate and_27, 8 bits wide
  Register register_1 (.D(or_1_out), .Q(register_1_q), .clk(or_1_out[1]), .clr(reset));  // open: en
  assign or_1_out = and_10_out | and_11_out;  // OR_Gate or_1, 8 bits wide
  assign or_2_out = and_12_out | and_13_out;  // OR_Gate or_2, 8 bits wide
  Register register_2 (.D(or_2_out), .Q(register_2_q), .clk(or_2_out[1]), .clr(reset));  // open: en
  Register register_3 (.D(or_3_out), .Q(register_3_q), .clk(or_3_out[1]), .clr(reset));  // open: en
  assign or_3_out = and_14_out | and_15_out;  // OR_Gate or_3, 8 bits wide
  assign or_4_out = and_16_out | and_17_out;  // OR_Gate or_4, 8 bits wide
  Register register_4 (.D(or_4_out), .Q(register_4_q), .clk(or_4_out[1]), .clr(reset));  // open: en
  assign or_5_out = and_18_out | and_19_out;  // OR_Gate or_5, 8 bits wide
  Register register_5 (.D(or_5_out), .Q(register_5_q), .clk(or_5_out[1]), .clr(reset));  // open: en
  Register register_6 (.D(or_6_out), .Q(register_6_q), .clk(or_6_out[1]), .clr(reset));  // open: en
  assign or_6_out = and_20_out | and_21_out;  // OR_Gate or_6, 8 bits wide
  Register register_7 (.D(or_7_out), .Q(register_7_q), .clk(or_7_out[1]), .clr(reset));  // open: en
  assign or_7_out = and_22_out | and_23_out;  // OR_Gate or_7, 8 bits wide
  assign or_8_out = and_24_out | and_25_out;  // OR_Gate or_8, 8 bits wide
  Register register_8 (.D(or_8_out), .Q(register_8_q), .clk(or_8_out[1]), .clr(reset));  // open: en
  assign or_9_out = and_26_out | and_27_out;  // OR_Gate or_9, 8 bits wide
  Register register_9 (.D(or_9_out), .Q(register_9_q), .clk(or_9_out[1]), .clr(reset));  // open: en
  Multiplexer #(.width(8), .disabled(0), .enable("false")) multiplexer_1 (
    .in1(register_1_q), .out(multiplexer_1_out), .sel(r0));  // open: in0
  Multiplexer #(.width(8), .disabled(0), .enable("false")) multiplexer_2 (
    .in1(register_2_q), .out(multiplexer_1_out), .sel(r1));  // open: in0
  Multiplexer #(.width(8), .disabled(0), .enable("false")) multiplexer_3 (
    .in1(register_3_q), .out(multiplexer_1_out), .sel(r2));  // open: in0
  Multiplexer #(.width(8), .disabled(0), .enable("false")) multiplexer_4 (
    .in1(register_4_q), .out(multiplexer_1_out), .sel(r3));  // open: in0
  Multiplexer #(.width(8), .disabled(0), .enable("false")) multiplexer_5 (
    .in1(register_5_q), .out(multiplexer_1_out), .sel(r4));  // open: in0
  Multiplexer #(.width(8), .disabled(0), .enable("false")) multiplexer_6 (
    .in1(register_6_q), .out(multiplexer_1_out), .sel(r5));  // open: in0
  Multiplexer #(.width(8), .disabled(0), .enable("false")) multiplexer_7 (
    .in1(register_7_q), .out(multiplexer_1_out), .sel(r6));  // open: in0
  Multiplexer #(.width(8), .disabled(0), .enable("false")) multiplexer_8 (
    .in1(register_8_q), .out(multiplexer_1_out), .sel(r7));  // open: in0
  Multiplexer #(.width(8), .disabled(0), .enable("false")) multiplexer_9 (
    .in1(register_9_q), .out(multiplexer_1_out), .sel(r8));  // open: in0
  assign to_cdm8 = decoder_1_out1 ? multiplexer_1_out : 8'bz;  // Controlled_Buffer controlled_buffer_1
  Decoder #(.disabled(0)) decoder_1 (.out1(decoder_1_out1), .sel(read_write), .en(write_state_to_cmd8));  // open: out0
  Decoder #(.select(4), .disabled(0), .enable("false")) decoder_2 (
    .out1(r0), .out2(r1), .out3(r2), .out4(r3), .out5(r4), .out6(r5), .out7(r6), .out8(r7), .out9(r8),
    .sel(counter_1_q));  // open: out0, out10, out11, out12, out13, out14, out15
  Counter #(.width(4), .max('h9)) counter_1 (
    .Q(counter_1_q), .clk(write_state_to_cmd8), .clr(reset));  // open: load, D, count, carry

  // Other names for the same wires on the sheet: _1v8[7:0] = {8{_1}}; _1v0 = _1_in[0]; _1v = _1_in[1];
  //   _1vv8[7:0] = {8{_1_in[1]}}; _2v8[7:0] = {8{_2}}; _2v0 = _2_in[0]; _2v = _2_in[1]; _2vv8[7:0] = {8{_2_in[1]}};
  //   _3v8[7:0] = {8{_3}}; _3v0 = _3_in[0]; _3v = _3_in[1]; _3vv8[7:0] = {8{_3_in[1]}}; _4v8[7:0] = {8{_4}};
  //   _4v0 = _4_in[0]; _4v = _4_in[1]; _4vv8[7:0] = {8{_4_in[1]}}; _5v8[7:0] = {8{_5}}; _5v0 = _5_in[0];
  //   _5v = _5_in[1]; _5vv8[7:0] = {8{_5_in[1]}}; _6v8[7:0] = {8{_6}}; _6v0 = _6_in[0]; _6v = _6_in[1];
  //   _6vv8[7:0] = {8{_6_in[1]}}; _7v8[7:0] = {8{_7}}; _7v0 = _7_in[0]; _7v = _7_in[1]; _7vv8[7:0] = {8{_7_in[1]}};
  //   _8v8[7:0] = {8{_8}}; _8v0 = _8_in[0]; _8v = _8_in[1]; _8vv8[7:0] = {8{_8_in[1]}}; _9v8[7:0] = {8{_9}};
  //   _9v0 = _9_in[0]; _9v = _9_in[1]; _9vv8[7:0] = {8{_9_in[1]}}; rest = reset

  // Notes on the sheet:
  //   O Cells
  //   X Cells
  //   const for X
  //   const for O
  //   КОСТЫЛИИИИИИИИИ
endmodule

module CDM8Turn (
  input  addr,
  input  write,
  input  [7:0] CDM8_input,
  output cell_1,
  output cell_2,
  output cell_3,
  output cell_4,
  output cell_5,
  output cell_6,
  output cell_7,
  output cell_8,
  output cell_9
);

  wire decoder_2_out0, decoder_2_out1, decoder_2_out2, decoder_2_out3, decoder_2_out4, decoder_2_out5,
       decoder_2_out6, decoder_2_out7, decoder_2_out8, enable;

  Decoder #(.disabled(0)) decoder_1 (.out0(enable), .sel(write), .en(addr));  // open: out1
  Decoder #(.select(4), .disabled(0), .enable("false")) decoder_2 (
    .out0(decoder_2_out0), .out1(decoder_2_out1), .out2(decoder_2_out2), .out3(decoder_2_out3),
    .out4(decoder_2_out4), .out5(decoder_2_out5), .out6(decoder_2_out6), .out7(decoder_2_out7),
    .out8(decoder_2_out8), .sel(CDM8_input[3:0]));  // open: out9, out10, out11, out12, out13, out14, out15
  assign cell_1 = enable ? decoder_2_out0 : 1'bz;  // Controlled_Buffer controlled_buffer_1
  Pull_Resistor pull_resistor_1 (.node(cell_1));
  assign cell_2 = enable ? decoder_2_out1 : 1'bz;  // Controlled_Buffer controlled_buffer_2
  Pull_Resistor pull_resistor_2 (.node(cell_2));
  Pull_Resistor pull_resistor_3 (.node(cell_3));
  assign cell_3 = enable ? decoder_2_out2 : 1'bz;  // Controlled_Buffer controlled_buffer_3
  Pull_Resistor pull_resistor_4 (.node(cell_4));
  assign cell_4 = enable ? decoder_2_out3 : 1'bz;  // Controlled_Buffer controlled_buffer_4
  assign cell_5 = enable ? decoder_2_out4 : 1'bz;  // Controlled_Buffer controlled_buffer_5
  Pull_Resistor pull_resistor_5 (.node(cell_5));
  assign cell_6 = enable ? decoder_2_out5 : 1'bz;  // Controlled_Buffer controlled_buffer_6
  Pull_Resistor pull_resistor_6 (.node(cell_6));
  Pull_Resistor pull_resistor_7 (.node(cell_7));
  assign cell_7 = enable ? decoder_2_out6 : 1'bz;  // Controlled_Buffer controlled_buffer_7
  assign cell_8 = enable ? decoder_2_out7 : 1'bz;  // Controlled_Buffer controlled_buffer_8
  Pull_Resistor pull_resistor_8 (.node(cell_8));
  assign cell_9 = enable ? decoder_2_out8 : 1'bz;  // Controlled_Buffer controlled_buffer_9
  Pull_Resistor pull_resistor_9 (.node(cell_9));
endmodule

module PlayerToCDM8 (
  input  addr,
  input  read,
  input  player,
  output [7:0] ToCDM8
);

  wire decoder_1_out1;

  Decoder #(.disabled(0)) decoder_1 (.out1(decoder_1_out1), .sel(read), .en(addr));  // open: out0
  assign ToCDM8 = decoder_1_out1 ? {{7{1'b0}}, player} : 8'bz;  // Controlled_Buffer controlled_buffer_1
endmodule
